# Fritzing sketch IRPi Breadboard Fritzing (saved by Fritzing 0.9.3b)
breadboards: 1

parts:
  Raspberry_Pi_1 = Raspberry Pi 3 [part_number=RPI-3-V1.2]
  R1 = Resistor [tolerance=±5% resistance=56 package="1206 [SMD]"]
  R3 = Resistor [tolerance=±5% resistance=1.8k package="0603 [SMD]"]
  S1 = Pushbutton [package="[THT]"]
  U1 = 555 Timer [package="SO8 [SMD]"]  # not connected
  D1 = LTE-302 [package=lte-302]
  R2 = Resistor [tolerance=±5% resistance=180 package="2512 [SMD]"]
  C2 = Ceramic Capacitor [capacitance=0.01µF package="0805 [SMD, multilayer]"]
  LED1 = LED - 5mm [color="Green (565nm)" package="5 mm [THT]"]
  R4 = Resistor [tolerance=±5% resistance=560 package="0603 [SMD]"]
  IR1 = TSOP312.., 314.. [package=THT]
  R5 = Resistor [tolerance=±5% resistance=560 package="0603 [SMD]"]
  D2 = LTE-302 [package=lte-302]  # not connected
  R6 = Resistor [tolerance=±5% resistance=560 package="0603 [SMD]"]  # not connected
  U2 = 555 Timer [package="SO8 [SMD]"]  # not connected
  IR2 = TSOP312.., 314.. [package=THT]  # not connected
  C3 = Ceramic Capacitor [capacitance=0.01µF package="0805 [SMD, multilayer]"]  # not connected
  LED2 = LED - 5mm [color="Green (565nm)" package="5 mm [THT]"]  # not connected
  S2 = Pushbutton [package="[THT]"]  # not connected

nets:
  N1: Raspberry_Pi_1.3v3, S1.Pin_1, S1.Pin_2, IR1.Data
  N2: Raspberry_Pi_1.GPIO17, LED1.anode
  N3: Raspberry_Pi_1.GPIO22, S1.Pin_3, S1.Pin_4, R5.Pin_0
  N4: Raspberry_Pi_1.GPIO26, IR1.GND
  N5: Raspberry_Pi_1.GND, IR1.Vs, R5.Pin_1
  N6: Raspberry_Pi_1.5V, R2.Pin_1
  N7: R1.Pin_0, D1.A
  N8: R3.Pin_0, C2.1
  N9: R3.Pin_1, R2.Pin_0
  N10: D1.C, C2.0, R4.Pin_0
  N11: LED1.cathode, R4.Pin_1
